# Fritzing sketch main_lights (saved by Fritzing 0.6.3b)
breadboards: 1

parts:
  Feed_from_battery = Power plug
  S1 = Pushbutton [package="[THT]"]
  Brake_light_left = LED - 5mm [color="Red (633nm)" package="5 mm [THT]"]
  Brake_light_right = LED - 5mm [color="Red (633nm)" package="5 mm [THT]"]
  Park_rear_right = LED - 5mm [color="Red (633nm)" package="5 mm [THT]"]
  Park_rear_left = LED - 5mm [color="Red (633nm)" package="5 mm [THT]"]
  Park_front_right = LED - 5mm [color="White (4500K)" package="5 mm [THT]"]
  Park_front_left = LED - 5mm [color="White (4500K)" package="5 mm [THT]"]
  Blinker_front_right = LED - 5mm [color="Orange (612nm)" package="5 mm [THT]"]
  Blinker_rear_right = LED - 5mm [color="Orange (612nm)" package="5 mm [THT]"]
  Q1 = Basic FET P-Channel [package="D2Pak [SMD]"]
  U1 = mystery part, 1 pin [chip_label=? spacing=300mil part_number="Blinker circuit"]
  Main_power_relay = Relay [package=THT]
  Headlight_short_right = LED - 5mm [color="White (8000K)" package="5 mm [THT]"]
  Headlight_short_left = LED - 5mm [color="White (8000K)" package="5 mm [THT]"]
  S2_Short/long_lights_sw = Toggle Switch [package=THT]
  Headlight_long_right = LED - 5mm [color="White (6500K)" package="5 mm [THT]"]
  Headlight_long_right_2 = LED - 5mm [color="White (6500K)" package="5 mm [THT]"]
  LED13 = LED - 5mm [color="Orange (612nm)" package="5 mm [THT]"]
  Blinker_rear_left = LED - 5mm [color="Orange (612nm)" package="5 mm [THT]"]
  Q2 = Basic FET P-Channel [package="D2Pak [SMD]"]
  Worklight_front_right = LED - 5mm [color="White (4500K)" package="5 mm [THT]"]
  Worklight_front_left = LED - 5mm [color="White (4500K)" package="5 mm [THT]"]
  S3_Worklight_switch_front = Toggle Switch [package=THT]
  Worklight_rear_left = LED - 5mm [color="White (4500K)" package="5 mm [THT]"]
  Worklight_rear_right = LED - 5mm [color="White (4500K)" package="5 mm [THT]"]
  S4_Worklight_switch_rear = Toggle Switch [package=THT]
  S2_Main_light_switch = Toggle Switch [package=THT]
  U2 = mystery part, 1 pin [chip_label=? spacing=300mil]

nets:
  N1: Feed_from_battery.VCC, Main_power_relay.C2
  GND: Feed_from_battery.GND, Brake_light_left.cathode, Brake_light_right.cathode, Park_rear_right.cathode, Park_rear_left.cathode, Park_front_right.cathode, Park_front_left.cathode, Blinker_front_right.cathode, Blinker_rear_right.cathode, Headlight_short_right.cathode, Headlight_short_left.cathode, Headlight_long_right.cathode, Headlight_long_right_2.cathode, LED13.cathode, Blinker_rear_left.cathode, Worklight_front_right.cathode, Worklight_front_left.cathode, Worklight_rear_left.cathode, Worklight_rear_right.cathode
  12V: S1.Pin_1, S1.Pin_2, Blinker_front_right.anode, Blinker_rear_right.anode, Q1.drain, Q1.source, Main_power_relay.B, Q2.source, S3_Worklight_switch_front.COM, S4_Worklight_switch_rear.COM, S2_Main_light_switch.COM
  N2: S1.Pin_3, S1.Pin_4, Brake_light_left.anode, Brake_light_right.anode
  N3: Park_rear_right.anode, Park_rear_left.anode, Park_front_right.anode, Park_front_left.anode, S2_Short/long_lights_sw.COM, S2_Main_light_switch.L1, S2_Main_light_switch.L2
  N4: Q1.Gate, U1.pin1, Q2.Gate, U2.pin1
  N5: Headlight_short_right.anode, Headlight_short_left.anode, S2_Short/long_lights_sw.L1
  N6: S2_Short/long_lights_sw.L2, Headlight_long_right.anode, Headlight_long_right_2.anode
  N7: LED13.anode, Blinker_rear_left.anode, Q2.drain
  N8: Worklight_front_right.anode, Worklight_front_left.anode, S3_Worklight_switch_front.L1
  N9: Worklight_rear_left.anode, Worklight_rear_right.anode, S4_Worklight_switch_rear.L1

notes:
  MF-Control, Basic circuit for driving, brake, park etc lights. Details at https://github.com/opensievi/MF-control, 0.1
